# Fritzing sketch Projeto Integrador 2015-1 (saved by Fritzing 0.9.1b)
breadboards: 1

parts:
  7404 = 7404 [package="DIP (Dual Inline) [THT]"]
  7_Segment1 = 7 Segment Display  # not connected
  Power_plug1 = Power plug
  A = Toggle Switch [package=THT]
  B = Toggle Switch [package=THT]
  C = Toggle Switch [package=THT]
  D = Toggle Switch [package=THT]

nets:
  A: 7404.1A, A.COM
  ¬A: 7404.1Y
  B: 7404.2A, B.COM
  ¬B: 7404.2Y
  GND: 7404.GND, Power_plug1.GND, A.L2, B.L2, C.L2, D.L2
  ¬C: 7404.4Y
  C: 7404.4A, C.COM
  ¬D: 7404.5Y
  D: 7404.5A, D.COM
  5V: 7404.VCC, Power_plug1.VCC, A.L1, B.L1, C.L1, D.L1

custom parts:
  7404: Hex Inverter
